# Fritzing sketch circuit_sketch (saved by Fritzing 0.9.3b)
breadboards: 1

parts:
  Part1 = Arduino Uno (Rev3) - ICSP
  SP1 = SPEAKER [package=pcb_mount_speaker]
  Q2 = npn-Powertransistor [package="TO220 [THT]"]
  R1 = Resistor [tolerance=±5% resistance=220 package=THT]

nets:
  N1: Part1.D9_PWM, R1.Pin_0
  N2: Part1.GND, Q2.emitter
  N3: Part1.5V, SP1.-
  N4: SP1.+, Q2.collector
  N5: Q2.base, R1.Pin_1
